// Digital circuit RV32I.dig as structural Verilog
module RV32I (
  input  CLC,
  input  [31:0] INSTR,
  input  NORMAL,
  input  RUN,
  input  CPU_HOLD,
  input  [31:0] MEM_R,
  output [31:0] INSTR_EXECUTE,
  output [31:0] INSTR_MEMORY,
  output [31:0] INSTR_WRITE,
  output GO,
  output [4:0] HELD_REGISTER_0,
  output [4:0] HELD_REGISTER_1,
  output [7:0] ALU_INSTR,
  output [31:0] ALU_A,
  output [31:0] ALU_B,
  output [31:0] ALU_Y,
  output COMP,
  output [23:0] PC,
  output CPU_SET_MEM_ADDRESS,
  output [23:0] MEM_ADDRESS,
  output CPU_WRITE_MEM,
  output [31:0] MEM_W,
  output ERROR
);

  wire ALU_SET_REGISTER, COMP_MEMORY, COMP_SET_REGISTER, EXECUTE_BRANCH_HOLD, INSTR_DECODE_EN,
       INSTR_EXECUTE_EN, INSTR_MEMORY_EN, JUMP, MEMORY_SET_REGISTER, or_1_out, PC_EN, PC_INC_SET_PC,
       PC_STALL, READ_RS1, READ_RS2, REG_WRITE, REGISTER_HOLD, rv32i_memory_control_1_memory_hold,
       rv32i_write_control_1_execute_hold, WRITE_RD;
  wire [4:0] RS1_A, RS2_A;
  wire [7:0] COMP_SEL;
  wire [23:0] driver_4_out, PC_EXECUTE, PC_IN, PC_INC_OUT;
  wire [30:0] pulldown_4_out;
  wire [31:0] driver_3_out, driver_6_out, driver_9_out, RESULT_WRITE, RS1, RS2, rv32i_alu_input_1_comp_a,
       rv32i_alu_input_1_comp_b;
  wire [31:24] driver_5_out, RESULT_MEMORY;

  nor nor_1 (GO, CPU_HOLD, REGISTER_HOLD, 1'b0, EXECUTE_BRANCH_HOLD, 1'b0);
  RV32I_Fetch_Control rv32i_fetch_control_1 (
    .Normal(NORMAL), .Run(RUN), .Go(GO), .JUMP(JUMP), .PC_EN(PC_EN), .PC_INC_SET_PC(PC_INC_SET_PC),
    .PC_STALL(PC_STALL));
  assign PC_IN = PC_STALL ? PC : 24'bz;  // Driver driver_1
  Register #(.Bits(24), .isProgramCounter("true")) u_PC (.D(PC_IN), .C(CLC), .en(PC_EN), .Q(PC));
  Add #(.Bits(24)) PC_INC (.a(PC), .b(24'h1), .c_i(1'b0), .s(PC_INC_OUT));  // open: c_o
  assign PC_IN = PC_INC_SET_PC ? PC_INC_OUT : 24'bz;  // Driver driver_2
  PullDown #(.Bits(24)) pulldown_1 (.out(PC_IN));
  RV32I_Decode_Control rv32i_decode_control_1 (
    .INSTR(INSTR), .Normal(NORMAL), .Run(RUN), .Go(GO), .DECODE_EN(INSTR_DECODE_EN), .WRITE_RD(WRITE_RD),
    .READ_RS1(READ_RS1), .READ_RS2(READ_RS2), .ERROR(ERROR));  // open: DECODE_HOLD
  RV32I_Register_Reserve rv32i_register_reserve_1 (
    .INSTR(INSTR), .CLC(CLC), .RD(WRITE_RD), .RS1(READ_RS1), .RS2(READ_RS2), .HOLD(REGISTER_HOLD),
    .E(HELD_REGISTER_0), .O(HELD_REGISTER_1));
  assign driver_3_out = GO ? INSTR : 32'bz;  // Driver driver_3
  PullDown #(.Bits(32)) pulldown_2 (.out(driver_3_out));
  assign driver_4_out = GO ? PC : 24'bz;  // Driver driver_4
  PullDown #(.Bits(24)) pulldown_3 (.out(driver_4_out));
  Register #(.Bits(32)) u_INSTR (.D(driver_3_out), .C(CLC), .en(INSTR_DECODE_EN), .Q(INSTR_EXECUTE));
  Register #(.Bits(24)) PC_2 (.D(driver_4_out), .C(CLC), .en(INSTR_DECODE_EN), .Q(PC_EXECUTE));
  // RV32I_Execute_Control rv32i_execute_control_1: pin names not known; wires that end beside it: INSTR_EXECUTE, NORMAL, RUN, COMP, EXECUTE_BRANCH_HOLD, INSTR_EXECUTE_EN, ALU_INSTR, COMP_SEL, RS1_A, RS2_A, JUMP
  RV32I_ALU_Input rv32i_alu_input_1 (
    .INSTR(INSTR_EXECUTE), .PC(PC_EXECUTE), .RS1(RS1), .RS2(RS2), .A(ALU_A), .B(ALU_B),
    .COMP_A(rv32i_alu_input_1_comp_a), .COMP_B(rv32i_alu_input_1_comp_b));
  RV32I_ALU ALU (.A(ALU_A), .B(ALU_B), .Y(ALU_Y), .O(ALU_INSTR));
  RV32I_Comparator rv32i_comparator_1 (
    .A(rv32i_alu_input_1_comp_a), .B(rv32i_alu_input_1_comp_b), .SEL(COMP_SEL), .Y(COMP));
  assign {driver_5_out, PC_IN} = JUMP ? ALU_Y : 32'bz;  // Driver driver_5
  Register #(.Bits(32)) INSTR_2 (.D(INSTR_EXECUTE), .C(CLC), .en(INSTR_EXECUTE_EN), .Q(INSTR_MEMORY));
  Register #(.Bits(32)) RESULT (.D(ALU_Y), .C(CLC), .en(1'b1), .Q({RESULT_MEMORY, MEM_ADDRESS}));
  Register u_COMP (.D(COMP), .C(CLC), .en(1'b1), .Q(COMP_MEMORY));
  Register #(.Bits(32)) u_RS2 (.D(RS2), .C(CLC), .en(1'b1), .Q(MEM_W));
  RV32I_Memory_Control rv32i_memory_control_1 (
    .INSTR(INSTR_MEMORY), .Normal(NORMAL), .Run(RUN), .MEMORY_HOLD(rv32i_memory_control_1_memory_hold),
    .MEMORY_EN(INSTR_MEMORY_EN), .ALU_SET_REGISTER(ALU_SET_REGISTER), .COMP_SET_REGISTER(COMP_SET_REGISTER),
    .MEMORY_SET_REGISTER(MEMORY_SET_REGISTER), .WRITE_TO_MEMORY(CPU_WRITE_MEM),
    .ACCESS_MEMORY(CPU_SET_MEM_ADDRESS));
  PullDown #(.Bits(31)) pulldown_4 (.out(pulldown_4_out));
  assign driver_6_out = ALU_SET_REGISTER ? {RESULT_MEMORY, MEM_ADDRESS} : 32'bz;  // Driver driver_6
  assign driver_6_out = COMP_SET_REGISTER ? {pulldown_4_out, COMP_MEMORY} : 32'bz;  // Driver driver_7
  assign driver_6_out = MEMORY_SET_REGISTER ? MEM_R : 32'bz;  // Driver driver_8
  Register #(.Bits(32)) INSTR_3 (.D(INSTR_MEMORY), .C(CLC), .en(INSTR_MEMORY_EN), .Q(INSTR_WRITE));
  Register #(.Bits(32)) RESULT_2 (.D(driver_6_out), .C(CLC), .en(1'b1), .Q(RESULT_WRITE));
  RV32I_Write_Control rv32i_write_control_1 (
    .INSTR(INSTR_WRITE), .Normal(NORMAL), .Run(RUN), .EXECUTE_HOLD(rv32i_write_control_1_execute_hold),
    .REG_WRITE(REG_WRITE));
  or or_1 (or_1_out, INSTR_WRITE[7], INSTR_WRITE[8], INSTR_WRITE[9], INSTR_WRITE[10], INSTR_WRITE[11]);
  assign driver_9_out = or_1_out ? RESULT_WRITE : 32'bz;  // Driver driver_9
  PullDown #(.Bits(32)) pulldown_5 (.out(driver_9_out));
  RegisterFile #(.AddrBits(5), .Bits(32)) registerfile_1 (
    .Din(driver_9_out), .we(REG_WRITE), .Rw(INSTR_WRITE[11:7]), .C(CLC), .Ra(RS1_A), .Rb(RS2_A), .Da(RS1),
    .Db(RS2));

  // Other names for the same wires on the sheet: ACCESS_MEMORY = CPU_SET_MEM_ADDRESS; INSTR_DECODE[31:0] = INSTR;
  //   PC_OUT[23:0] = PC; RESULT_MEMORY[23:0] = MEM_ADDRESS; RS2_MEMORY[31:0] = MEM_W; WRITE_TO_MEMORY = CPU_WRITE_MEM

  // Notes on the sheet:
  //   CLC: Hz: 10
endmodule
